// Logisim project Traffic_light 3.circ as structural Verilog: 1 circuit, main circuit main
module main (
);

  wire and_1_out, and_2_out, and_3_out, and_4_out, clock_1_out, d_ff_1_q, d_ff_1_qn, d_ff_2_q, d_ff_2_qn,
       d_ff_3_q, d_ff_3_qn, d_ff_4_q, d_ff_4_qn, xor_1_out, xor_2_out;

  Clock clock_1 (.out(clock_1_out));
  xor xor_1 (xor_1_out, d_ff_1_q, d_ff_2_q);
  D_Flip_Flop d_ff_1 (.D(xor_1_out), .clk(clock_1_out), .Q(d_ff_1_q), .Qn(d_ff_1_qn));  // open: preset, reset
  D_Flip_Flop d_ff_2 (.D(d_ff_2_qn), .clk(clock_1_out), .Q(d_ff_2_q), .Qn(d_ff_2_qn));  // open: preset, reset
  and and_1 (and_1_out, d_ff_1_q, d_ff_2_qn);
  LED led_1 (.in(d_ff_1_q));
  LED led_2 (.in(d_ff_2_q));
  and and_2 (and_2_out, d_ff_1_qn, d_ff_2_qn);
  LED led_3 (.in(and_2_out));
  LED led_4 (.in(d_ff_1_qn));
  LED led_5 (.in(d_ff_2_q));
  LED led_6 (.in(and_1_out));
  LED led_7 (.in(d_ff_3_qn));
  LED led_8 (.in(d_ff_4_q));
  LED led_9 (.in(and_3_out));
  LED led_10 (.in(d_ff_3_q));
  LED led_11 (.in(d_ff_4_q));
  LED led_12 (.in(and_4_out));
  xor xor_2 (xor_2_out, d_ff_3_q, d_ff_4_q);
  D_Flip_Flop d_ff_3 (.D(xor_2_out), .clk(clock_1_out), .Q(d_ff_3_q), .Qn(d_ff_3_qn));  // open: preset, reset
  D_Flip_Flop d_ff_4 (.D(d_ff_4_qn), .clk(clock_1_out), .Q(d_ff_4_q), .Qn(d_ff_4_qn));  // open: preset, reset
  and and_3 (and_3_out, d_ff_3_q, d_ff_4_qn);
  and and_4 (and_4_out, d_ff_3_qn, d_ff_4_qn);

  // Notes on the sheet:
  //   q1
  //   q0
  //   r3(pair 2)
  //   y3(pair 2)
  //   g3(pair 2)
  //   r2(pair 1)
  //   y2(pair 1)
  //   g2(pair 1)
  //   r1(pair 1)
  //   y1(pair 1)
  //   g1(pair 1)
  //   r4(pair 2)
  //   y4(pair 2)
  //   g4(pair 2)
  //   q1
  //   q0
endmodule
